// Logisim project ByteForge_4.circ as structural Verilog: 2 circuits, main circuit ByteForge4
module ByteForge4 (
  input  [3:0] in_1,
  input  in_2,
  output [3:0] out_3
);

  wire clock_1_out;

  Clock clock_1 (.out(clock_1_out));
  REG4v2 reg4v2_1 (.D(in_1), .load(in_2), .clk(clock_1_out), .Q(out_3));
endmodule

module REG4v2 (
  input  [3:0] D,
  input  load,
  input  clk,
  output [3:0] Q
);

  wire multiplexer_1_out, multiplexer_2_out, multiplexer_3_out, multiplexer_4_out;

  D_Flip_Flop FF3 (.D(multiplexer_1_out), .clk(clk), .Q(Q[3]));  // open: Qn, preset, reset
  Multiplexer multiplexer_1 (.in0(Q[3]), .in1(D[3]), .out(multiplexer_1_out), .sel(load));
  Multiplexer multiplexer_2 (.in0(Q[2]), .in1(D[2]), .out(multiplexer_2_out), .sel(load));
  D_Flip_Flop FF2 (.D(multiplexer_2_out), .clk(clk), .Q(Q[2]));  // open: Qn, preset, reset
  Multiplexer multiplexer_3 (.in0(Q[1]), .in1(D[1]), .out(multiplexer_3_out), .sel(load));
  D_Flip_Flop FF1 (.D(multiplexer_3_out), .clk(clk), .Q(Q[1]));  // open: Qn, preset, reset
  Multiplexer multiplexer_4 (.in0(Q[0]), .in1(D[0]), .out(multiplexer_4_out), .sel(load));
  D_Flip_Flop FF0 (.D(multiplexer_4_out), .clk(clk), .Q(Q[0]));  // open: Qn, preset, reset
endmodule
